# Fritzing sketch NeoSectional_Schematic (saved by Fritzing 0.9.4)
circuit board: 10cm x 6cm
breadboards: 1

parts:
  J1 = Power Jack [package=power_jack_slot]
  IC1 = Voltage Regulator [package=78xxl]
  R2 = Resistor [tolerance=±5% resistance=10k package=THT]
  NEOPIXEL1 = Neopixel Strip -- White (30/m)
  C2 = Electrolytic Capacitor [capacitance=10μF package="0605 [SMD, electrolytic]"]
  C1 = Electrolytic Capacitor [capacitance=1000μF package="1010 [SMD, electrolytic]"]
  U1 = NodeMCU V1.0
  R3 = Resistor [tolerance=±5% resistance=10k package=THT]
  S1 = Toggle Switch [package=THT]

nets:
  GND: J1.GND, IC1.GND, NEOPIXEL1.GND, C2.-, C1.-, U1.GND, R3.Pin_0
  N1: J1.PWR, IC1.IN, C1.+
  +5V: IC1.OUT, NEOPIXEL1.+5V, C2.+, U1.Vin
  N2: R2.Pin_0, NEOPIXEL1.DO
  N3: R2.Pin_1, U1.D1
  N4: U1.D0, S1.L1
  N5: U1.D2, R3.Pin_1
  N6: U1.3V3, S1.COM

custom parts:
  Neopixel Strip -- White (30/m): Neopixel Strip, White, 30 pixels per meter.
  NodeMCU V1.0: ESP8266 based NodeMCU
